// Logisim project MIC-1.circ as structural Verilog: 22 circuits, main circuit main
module main (
  input  CLK,
  output [31:0] PC,
  output [8:0] MPC,
  output [31:0] B,
  output [31:0] C
);

  wire data_path_1_p8, data_path_1_p9, data_path_1_p10, data_path_1_p11, data_path_1_p12, data_path_1_p13,
       data_path_1_p14, data_path_1_p15, data_path_1_p16, data_path_1_p24, data_path_1_p25, data_path_1_p26,
       data_path_1_p27, data_path_1_p28, data_path_1_p29, data_path_1_p30, data_path_1_p31, data_path_1_p32,
       data_path_1_p34, data_path_1_p35, RESET_out;
  wire [1:0] data_path_1_p21, data_path_1_p38;
  wire [2:0] data_path_1_p7;
  wire [3:0] data_path_1_p17;
  wire [7:0] data_path_1_p33, mem_1_mem_fetch;
  wire [31:0] data_path_1_p1, data_path_1_p2, mem_1_mrm_rd;

  Mem mem_1 (
    .MEM_ADDR_32(data_path_1_p1), .CLK(CLK), .MEM_WR(data_path_1_p2), .MRM_RD(mem_1_mrm_rd),
    .MEM_FETCH(mem_1_mem_fetch), .wr(data_path_1_p7[2]), .rd(data_path_1_p7[1]), .fetch(data_path_1_p7[0]),
    .MEM_ADDR_8(PC));
  Button RESET (.out(RESET_out));
  // Data_Path data_path_1: pin names not known; wires that end beside it: data_path_1_p1, data_path_1_p2, mem_1_mrm_rd, data_path_1_p7[1], PC, mem_1_mem_fetch, data_path_1_p7[0], data_path_1_p8, data_path_1_p9, data_path_1_p10, data_path_1_p11, data_path_1_p12, data_path_1_p13, data_path_1_p14, data_path_1_p15, data_path_1_p16, data_path_1_p17[0], data_path_1_p17[1], data_path_1_p17[2], data_path_1_p17[3], data_path_1_p21, CLK, RESET_out, data_path_1_p24, data_path_1_p25, data_path_1_p26, data_path_1_p27, data_path_1_p28, data_path_1_p29, data_path_1_p30, data_path_1_p31, data_path_1_p32, data_path_1_p33, data_path_1_p34, data_path_1_p35, B, C, data_path_1_p38[0], data_path_1_p38[1]
  Control_Unit control_unit_1 (
    .CLK(CLK), .RESET(RESET_out), .MBR(data_path_1_p33), .N(data_path_1_p34), .Z(data_path_1_p35), .MPC(MPC),
    .MDR_B(data_path_1_p24), .PC_B(data_path_1_p25), .MBR_B(data_path_1_p26), .MBRU_B(data_path_1_p27),
    .SP_B(data_path_1_p28), .LV_B(data_path_1_p29), .CPP_B(data_path_1_p30), .TOS_B(data_path_1_p31),
    .OPC_B(data_path_1_p32), .Mem(data_path_1_p7), .ALU({data_path_1_p21, data_path_1_p17}),
    .Shifter(data_path_1_p38), .H_C(data_path_1_p16), .OPC_C(data_path_1_p15), .TOS_C(data_path_1_p14),
    .CPP_C(data_path_1_p13), .LV_C(data_path_1_p12), .SP_C(data_path_1_p11), .PC_C(data_path_1_p10),
    .MDR_C(data_path_1_p9), .MAR_C(data_path_1_p8));
endmodule

module Mem (
  input  wr,
  input  [31:0] MEM_WR,
  input  [31:0] MEM_ADDR_32,
  input  rd,
  input  [31:0] MEM_ADDR_8,
  input  fetch,
  input  CLK,
  output [31:0] MRM_RD,
  output [7:0] MEM_FETCH
);

  wire not_1_out, not_2_out, not_3_out;
  wire [7:0] ram_2_data;
  wire [31:0] ram_1_data;

  not not_1 (not_1_out, CLK);
  not not_2 (not_2_out, wr);
  RAM #(.addrWidth(24), .dataWidth(32)) ram_1 (
    .addr(MEM_ADDR_32[23:0]), .data(ram_1_data), .sel(1'b1), .clk(not_1_out), .ld(not_2_out), .clr(1'b0));
  assign ram_1_data = wr ? MEM_WR : 32'bz;  // Controlled_Buffer controlled_buffer_1
  assign MRM_RD = rd ? ram_1_data : 32'bz;  // Controlled_Buffer controlled_buffer_2
  not not_3 (not_3_out, CLK);
  assign MEM_FETCH = fetch ? ram_2_data : 8'bz;  // Controlled_Buffer controlled_buffer_3
  RAM #(.addrWidth(24)) ram_2 (
    .addr(MEM_ADDR_8[23:0]), .data(ram_2_data), .sel(1'b1), .clk(not_3_out), .clr(1'b0));  // open: ld

  // Notes on the sheet:
  //   Una truchada porque Logisim no tiene
  //   un bloque de memoria con dos canales de datos
endmodule

module Control_Unit (
  input  CLK,
  input  RESET,
  input  [7:0] MBR,
  input  N,
  input  Z,
  output [8:0] MPC,
  output MDR_B,
  output PC_B,
  output MBR_B,
  output MBRU_B,
  output SP_B,
  output LV_B,
  output CPP_B,
  output TOS_B,
  output OPC_B,
  output [2:0] Mem,
  output [5:0] ALU,
  output [1:0] Shifter,
  output H_C,
  output OPC_C,
  output TOS_C,
  output CPP_C,
  output LV_C,
  output SP_C,
  output PC_C,
  output MDR_C,
  output MAR_C
);

  wire and_1_out, and_2_out, d_flipflop_asc_1_q, d_flipflop_asc_2_q, not_1_out;
  wire [2:0] mir_1_jam;
  wire [3:0] control_store_1_cs_s4, mir_1_b;
  wire [7:0] mir_1_addr, multiplexer_3_out, or_2_out;
  wire [8:0] multiplexer_1_out, multiplexer_2_out;
  wire [8:8] mir_1_addr_2, or_1_out;
  wire [31:0] control_store_1_cs_s32;

  Multiplexer #(.width(9), .enable("false")) multiplexer_1 (
    .in0({9{1'b1}}), .in1(9'hff), .out(multiplexer_1_out), .sel(RESET));
  Multiplexer #(.width(9), .enable("false")) multiplexer_2 (
    .in0({9{1'b1}}), .in1(9'h100), .out(multiplexer_2_out), .sel(RESET));
  and and_1 (and_1_out, d_flipflop_asc_1_q, mir_1_jam[1]);
  D_FlipFlop_Asc d_flipflop_asc_1 (
    .nPRE(1'b1), .D(N), .Q(d_flipflop_asc_1_q), .CLK(CLK), .nCLR(not_1_out));  // open: nQ
  D_FlipFlop_Asc d_flipflop_asc_2 (
    .nPRE(1'b1), .D(Z), .Q(d_flipflop_asc_2_q), .CLK(CLK), .nCLR(not_1_out));  // open: nQ
  Multiplexer #(.width(8), .enable("false")) multiplexer_3 (
    .in0(mir_1_addr), .in1(or_2_out), .out(multiplexer_3_out), .sel(mir_1_jam[2]));
  or or_1 (or_1_out[8], and_1_out, and_2_out, mir_1_addr_2[8]);
  and and_2 (and_2_out, d_flipflop_asc_2_q, mir_1_jam[0]);
  assign or_2_out = MBR | mir_1_addr;  // OR_Gate or_2, 8 bits wide
  not not_1 (not_1_out, RESET);
  MPC mpc_1 (
    .Entrada({or_1_out[8], multiplexer_3_out}), .CLK(CLK), .Salida(MPC), .nPRE(multiplexer_1_out),
    .nCLR(multiplexer_2_out));
  Control_Store control_store_1 (.CS_E(MPC), .CS_S32(control_store_1_cs_s32), .CS_S4(control_store_1_cs_s4));
  MIR mir_1 (
    .Entrada_4(control_store_1_cs_s4), .Entrada_32(control_store_1_cs_s32), .CLK(CLK), .RESET(RESET),
    .B(mir_1_b), .Mem(Mem), .C({H_C, OPC_C, TOS_C, CPP_C, LV_C, SP_C, PC_C, MDR_C, MAR_C}),
    .ALU({Shifter, ALU}), .JAM(mir_1_jam), .Addr({mir_1_addr_2[8], mir_1_addr}));
  Decoder #(.select(4), .enable("false")) decoder_1 (
    .out0(MDR_B), .out1(PC_B), .out2(MBR_B), .out3(MBRU_B), .out4(SP_B), .out5(LV_B), .out6(CPP_B),
    .out7(TOS_B), .out8(OPC_B), .sel(mir_1_b));  // open: out9, out10, out11, out12, out13, out14, out15
endmodule

module Control_Store (
  input  [8:0] CS_E,
  output [31:0] CS_S32,
  output [3:0] CS_S4
);

  ROM #(.addrWidth(9), .dataWidth(32)) rom_1 (.addr(CS_E), .data(CS_S32), .sel(1'b1));
  ROM #(.addrWidth(9), .dataWidth(4)) rom_2 (.addr(CS_E), .data(CS_S4), .sel(1'b1));

  // Notes on the sheet:
  //   Otra truchada porque Logisim no tiene
  //   un bloque de memoria mas ancho que 32 bits
  //   contents of rom_1 (hex, n*v repeats v):
  //   80000000 255*0 435021
  //   contents of rom_2 (hex, n*v repeats v):
  //   f 255*0 1
endmodule

module MPC (
  input  [8:0] nPRE,
  input  [8:0] Entrada,
  input  CLK,
  input  [8:0] nCLR,
  output [8:0] Salida
);

  D_Latch d_latch_1 (.nPRE(nPRE[8]), .D(Entrada[8]), .Q(Salida[8]), .CLK(CLK), .nCLR(nCLR[8]));  // open: nQ
  D_Latch d_latch_2 (.nPRE(nPRE[7]), .D(Entrada[7]), .Q(Salida[7]), .CLK(CLK), .nCLR(nCLR[7]));  // open: nQ
  D_Latch d_latch_3 (.nPRE(nPRE[6]), .D(Entrada[6]), .Q(Salida[6]), .CLK(CLK), .nCLR(nCLR[6]));  // open: nQ
  D_Latch d_latch_4 (.nPRE(nPRE[5]), .D(Entrada[5]), .Q(Salida[5]), .CLK(CLK), .nCLR(nCLR[5]));  // open: nQ
  D_Latch d_latch_5 (.nPRE(nPRE[4]), .D(Entrada[4]), .Q(Salida[4]), .CLK(CLK), .nCLR(nCLR[4]));  // open: nQ
  D_Latch d_latch_6 (.nPRE(nPRE[3]), .D(Entrada[3]), .Q(Salida[3]), .CLK(CLK), .nCLR(nCLR[3]));  // open: nQ
  D_Latch d_latch_7 (.nPRE(nPRE[2]), .D(Entrada[2]), .Q(Salida[2]), .CLK(CLK), .nCLR(nCLR[2]));  // open: nQ
  D_Latch d_latch_8 (.nPRE(nPRE[1]), .D(Entrada[1]), .Q(Salida[1]), .CLK(CLK), .nCLR(nCLR[1]));  // open: nQ
  D_Latch d_latch_9 (.nPRE(nPRE[0]), .D(Entrada[0]), .Q(Salida[0]), .CLK(CLK), .nCLR(nCLR[0]));  // open: nQ
endmodule

module MIR (
  input  [3:0] Entrada_4,
  input  [31:0] Entrada_32,
  input  CLK,
  input  RESET,
  output [3:0] B,
  output [2:0] Mem,
  output [8:0] C,
  output [7:0] ALU,
  output [2:0] JAM,
  output [8:0] Addr
);

  wire [3:0] multiplexer_2_out, multiplexer_4_out, not_2_out;
  wire [31:0] multiplexer_1_out, multiplexer_3_out, not_1_out;

  Multiplexer #(.width(32), .enable("false")) multiplexer_1 (
    .in0({32{1'b1}}), .in1(not_1_out), .out(multiplexer_1_out), .sel(RESET));
  assign not_1_out = ~32'h435021;  // NOT_Gate not_1, 32 bits wide
  assign not_2_out = ~4'b0001;  // NOT_Gate not_2, 4 bits wide
  Multiplexer #(.width(4), .enable("false")) multiplexer_2 (
    .in0(4'b1111), .in1(not_2_out), .out(multiplexer_2_out), .sel(RESET));
  Multiplexer #(.width(32), .enable("false")) multiplexer_3 (
    .in0({32{1'b1}}), .in1(32'h435021), .out(multiplexer_3_out), .sel(RESET));
  Multiplexer #(.width(4), .enable("false")) multiplexer_4 (
    .in0(4'b1111), .in1(4'b0001), .out(multiplexer_4_out), .sel(RESET));
  Register_32_bits_Des register_32_bits_des_1 (
    .Entrada(Entrada_32), .CLK(CLK), .Salida({Addr, JAM, ALU, C, Mem}), .nPRE(multiplexer_1_out),
    .nCLR(multiplexer_3_out));
  Register_4_bits_Des register_4_bits_des_1 (
    .Entrada(Entrada_4), .CLK(CLK), .Salida(B), .nPRE(multiplexer_2_out), .nCLR(multiplexer_4_out));
endmodule

module Data_Path (
  input  MAR_C,
  input  [31:0] MEM_RD,
  input  MDR_C,
  input  MDR_B,
  input  rd,
  input  PC_C,
  input  [7:0] MEM_FETCH,
  input  PC_B,
  input  fetch,
  input  MBR,
  input  MBRU,
  input  SP_C,
  input  SP_B,
  input  LV_C,
  input  LV_B,
  input  CPP_C,
  input  CPP_B,
  input  TOS_C,
  input  RESET,
  input  TOS_B,
  input  OPC_C,
  input  OPC_B,
  input  H_C,
  input  INVA,
  input  ENA,
  input  CLK,
  input  ENB,
  input  INC,
  input  [1:0] F,
  input  SRA1,
  input  SLL8,
  output [31:0] MEM_MAR,
  output [31:0] MEM_WR,
  output [31:0] MEM_PC,
  output [7:0] OP_CODE,
  output [31:0] B,
  output N,
  output Z,
  output [31:0] C
);

  wire [7:0] multiplexer_1_out;
  wire [31:0] alu_32_bit_1_output, multiplexer_2_out, multiplexer_3_out,
       register_32_bits_hold_paralel_load_1_salida, register_32_bits_hold_paralel_load_4_salida,
       register_32_bits_hold_paralel_load_5_salida, register_32_bits_hold_paralel_load_6_salida,
       register_32_bits_hold_paralel_load_7_salida, register_32_bits_hold_paralel_load_8_salida,
       register_32_bits_hold_paralel_load_9_salida;

  Multiplexer #(.width(8), .enable("false")) multiplexer_1 (
    .in0({8{1'b1}}), .in1({8{1'b0}}), .out(multiplexer_1_out), .sel(RESET));
  Multiplexer #(.width(32), .enable("false")) multiplexer_2 (
    .in0({32{1'b1}}), .in1({32{1'b0}}), .out(multiplexer_2_out), .sel(RESET));
  Multiplexer #(.width(32), .enable("false")) multiplexer_3 (.in0(C), .in1(MEM_RD), .out(multiplexer_3_out), .sel(rd));
  Register_32_bits_Hold___Paralel_Load register_32_bits_hold_paralel_load_1 (
    .nPRE({32{1'b1}}), .Salida(register_32_bits_hold_paralel_load_1_salida), .Entrada(C),
    .nCLR(multiplexer_2_out), .LOAD(MAR_C), .CLK(CLK));
  Register_8_bits_Hold___Paralel_Load register_8_bits_hold_paralel_load_1 (
    .nPRE({8{1'b1}}), .Salida(OP_CODE), .Entrada(MEM_FETCH), .LOAD(fetch), .nCLR(multiplexer_1_out), .CLK(CLK));
  MAR mar_1 (.inp(register_32_bits_hold_paralel_load_1_salida), .out(MEM_MAR));
  Register_32_bits_Hold___Paralel_Load register_32_bits_hold_paralel_load_2 (
    .nPRE({32{1'b1}}), .Salida(MEM_WR), .Entrada(multiplexer_3_out), .nCLR(multiplexer_2_out), .LOAD(MDR_C),
    .CLK(CLK));
  Register_32_bits_Hold___Paralel_Load register_32_bits_hold_paralel_load_3 (
    .nPRE({32{1'b1}}), .Salida(MEM_PC), .Entrada(C), .nCLR(multiplexer_2_out), .LOAD(PC_C), .CLK(CLK));
  Register_32_bits_Hold___Paralel_Load register_32_bits_hold_paralel_load_4 (
    .nPRE({32{1'b1}}), .Salida(register_32_bits_hold_paralel_load_4_salida), .Entrada(C),
    .nCLR(multiplexer_2_out), .LOAD(SP_C), .CLK(CLK));
  Register_32_bits_Hold___Paralel_Load register_32_bits_hold_paralel_load_5 (
    .nPRE({32{1'b1}}), .Salida(register_32_bits_hold_paralel_load_5_salida), .Entrada(C),
    .nCLR(multiplexer_2_out), .LOAD(LV_C), .CLK(CLK));
  Register_32_bits_Hold___Paralel_Load register_32_bits_hold_paralel_load_6 (
    .nPRE({32{1'b1}}), .Salida(register_32_bits_hold_paralel_load_6_salida), .Entrada(C),
    .nCLR(multiplexer_2_out), .LOAD(CPP_C), .CLK(CLK));
  Register_32_bits_Hold___Paralel_Load register_32_bits_hold_paralel_load_7 (
    .nPRE({32{1'b1}}), .Salida(register_32_bits_hold_paralel_load_7_salida), .Entrada(C),
    .nCLR(multiplexer_2_out), .LOAD(TOS_C), .CLK(CLK));
  Register_32_bits_Hold___Paralel_Load register_32_bits_hold_paralel_load_8 (
    .nPRE({32{1'b1}}), .Salida(register_32_bits_hold_paralel_load_8_salida), .Entrada(C),
    .nCLR(multiplexer_2_out), .LOAD(OPC_C), .CLK(CLK));
  Register_32_bits_Hold___Paralel_Load register_32_bits_hold_paralel_load_9 (
    .nPRE({32{1'b1}}), .Salida(register_32_bits_hold_paralel_load_9_salida), .Entrada(C),
    .nCLR(multiplexer_2_out), .LOAD(H_C), .CLK(CLK));
  ALU_32_bit alu_32_bit_1 (
    .A(register_32_bits_hold_paralel_load_9_salida), .Cin(INC), .F0(F[0]), .F1(F[1]), .ENB(ENB), .ENA(ENA),
    .INVA(INVA), .B(B), .Z(Z), .Output(alu_32_bit_1_output), .N(N));  // open: Cout
  MBR_EN mbr_en_1 (.in_1(OP_CODE), .Salida_Signada(B), .Salida_No_Signada(B), .MRB(MBR), .MBRU(MBRU));
  Desplazador desplazador_1 (.Entrada(alu_32_bit_1_output), .SRA1(SRA1), .SLL8(SLL8), .Salida(C));
  assign B = MDR_B ? MEM_WR : 32'bz;  // Controlled_Buffer controlled_buffer_1
  assign B = PC_B ? MEM_PC : 32'bz;  // Controlled_Buffer controlled_buffer_2
  assign B = SP_B ? register_32_bits_hold_paralel_load_4_salida : 32'bz;  // Controlled_Buffer controlled_buffer_3
  assign B = LV_B ? register_32_bits_hold_paralel_load_5_salida : 32'bz;  // Controlled_Buffer controlled_buffer_4
  assign B = CPP_B ? register_32_bits_hold_paralel_load_6_salida : 32'bz;  // Controlled_Buffer controlled_buffer_5
  assign B = TOS_B ? register_32_bits_hold_paralel_load_7_salida : 32'bz;  // Controlled_Buffer controlled_buffer_6
  assign B = OPC_B ? register_32_bits_hold_paralel_load_8_salida : 32'bz;  // Controlled_Buffer controlled_buffer_7

  // Notes on the sheet:
  //   Preset 8 Bits
  //   Clear 8 Bits
  //   Preset 32 Bits
  //   Clear 32 Bits
  //   Bus C
  //   Bus B
endmodule

module Register_32_bits_Hold___Paralel_Load (
  input  [31:0] nPRE,
  input  [31:0] Entrada,
  input  [31:0] nCLR,
  input  LOAD,
  input  CLK,
  output [31:0] Salida
);

  wire [31:0] multiplexer_1_out;

  Multiplexer #(.width(32), .enable("false")) multiplexer_1 (
    .in1(Entrada), .out(multiplexer_1_out), .sel(LOAD));  // open: in0
  Register_32_bits_Des register_32_bits_des_1 (
    .Entrada(multiplexer_1_out), .CLK(CLK), .Salida(Salida), .nPRE(nPRE), .nCLR(nCLR));
endmodule

module Register_32_bits_Des (
  input  [31:0] nPRE,
  input  [31:0] Entrada,
  input  CLK,
  input  [31:0] nCLR,
  output [31:0] Salida
);

  D_FlipFlop_Des d_flipflop_des_1 (
    .D(Entrada[31]), .CLK(CLK), .Q(Salida[31]), .nPRE(nPRE[31]), .nCLR(nCLR[31]));  // open: nQ
  D_FlipFlop_Des d_flipflop_des_2 (
    .D(Entrada[30]), .CLK(CLK), .Q(Salida[30]), .nPRE(nPRE[30]), .nCLR(nCLR[30]));  // open: nQ
  D_FlipFlop_Des d_flipflop_des_3 (
    .D(Entrada[29]), .CLK(CLK), .Q(Salida[29]), .nPRE(nPRE[29]), .nCLR(nCLR[29]));  // open: nQ
  D_FlipFlop_Des d_flipflop_des_4 (
    .D(Entrada[28]), .CLK(CLK), .Q(Salida[28]), .nPRE(nPRE[28]), .nCLR(nCLR[28]));  // open: nQ
  D_FlipFlop_Des d_flipflop_des_5 (
    .D(Entrada[27]), .CLK(CLK), .Q(Salida[27]), .nPRE(nPRE[27]), .nCLR(nCLR[27]));  // open: nQ
  D_FlipFlop_Des d_flipflop_des_6 (
    .D(Entrada[26]), .CLK(CLK), .Q(Salida[26]), .nPRE(nPRE[26]), .nCLR(nCLR[26]));  // open: nQ
  D_FlipFlop_Des d_flipflop_des_7 (
    .D(Entrada[25]), .CLK(CLK), .Q(Salida[25]), .nPRE(nPRE[25]), .nCLR(nCLR[25]));  // open: nQ
  D_FlipFlop_Des d_flipflop_des_8 (
    .D(Entrada[24]), .CLK(CLK), .Q(Salida[24]), .nPRE(nPRE[24]), .nCLR(nCLR[24]));  // open: nQ
  D_FlipFlop_Des d_flipflop_des_9 (
    .D(Entrada[23]), .CLK(CLK), .Q(Salida[23]), .nPRE(nPRE[23]), .nCLR(nCLR[23]));  // open: nQ
  D_FlipFlop_Des d_flipflop_des_10 (
    .D(Entrada[22]), .CLK(CLK), .Q(Salida[22]), .nPRE(nPRE[22]), .nCLR(nCLR[22]));  // open: nQ
  D_FlipFlop_Des d_flipflop_des_11 (
    .D(Entrada[21]), .CLK(CLK), .Q(Salida[21]), .nPRE(nPRE[21]), .nCLR(nCLR[21]));  // open: nQ
  D_FlipFlop_Des d_flipflop_des_12 (
    .D(Entrada[20]), .CLK(CLK), .Q(Salida[20]), .nPRE(nPRE[20]), .nCLR(nCLR[20]));  // open: nQ
  D_FlipFlop_Des d_flipflop_des_13 (
    .D(Entrada[19]), .CLK(CLK), .Q(Salida[19]), .nPRE(nPRE[19]), .nCLR(nCLR[19]));  // open: nQ
  D_FlipFlop_Des d_flipflop_des_14 (
    .D(Entrada[18]), .CLK(CLK), .Q(Salida[18]), .nPRE(nPRE[18]), .nCLR(nCLR[18]));  // open: nQ
  D_FlipFlop_Des d_flipflop_des_15 (
    .D(Entrada[17]), .CLK(CLK), .Q(Salida[17]), .nPRE(nPRE[17]), .nCLR(nCLR[17]));  // open: nQ
  D_FlipFlop_Des d_flipflop_des_16 (
    .D(Entrada[16]), .CLK(CLK), .Q(Salida[16]), .nPRE(nPRE[16]), .nCLR(nCLR[16]));  // open: nQ
  D_FlipFlop_Des d_flipflop_des_17 (
    .D(Entrada[15]), .CLK(CLK), .Q(Salida[15]), .nPRE(nPRE[15]), .nCLR(nCLR[15]));  // open: nQ
  D_FlipFlop_Des d_flipflop_des_18 (
    .D(Entrada[14]), .CLK(CLK), .Q(Salida[14]), .nPRE(nPRE[14]), .nCLR(nCLR[14]));  // open: nQ
  D_FlipFlop_Des d_flipflop_des_19 (
    .D(Entrada[13]), .CLK(CLK), .Q(Salida[13]), .nPRE(nPRE[13]), .nCLR(nCLR[13]));  // open: nQ
  D_FlipFlop_Des d_flipflop_des_20 (
    .D(Entrada[12]), .CLK(CLK), .Q(Salida[12]), .nPRE(nPRE[12]), .nCLR(nCLR[12]));  // open: nQ
  D_FlipFlop_Des d_flipflop_des_21 (
    .D(Entrada[11]), .CLK(CLK), .Q(Salida[11]), .nPRE(nPRE[11]), .nCLR(nCLR[11]));  // open: nQ
  D_FlipFlop_Des d_flipflop_des_22 (
    .D(Entrada[10]), .CLK(CLK), .Q(Salida[10]), .nPRE(nPRE[10]), .nCLR(nCLR[10]));  // open: nQ
  D_FlipFlop_Des d_flipflop_des_23 (
    .D(Entrada[9]), .CLK(CLK), .Q(Salida[9]), .nPRE(nPRE[9]), .nCLR(nCLR[9]));  // open: nQ
  D_FlipFlop_Des d_flipflop_des_24 (
    .D(Entrada[8]), .CLK(CLK), .Q(Salida[8]), .nPRE(nPRE[8]), .nCLR(nCLR[8]));  // open: nQ
  D_FlipFlop_Des d_flipflop_des_25 (
    .D(Entrada[7]), .CLK(CLK), .Q(Salida[7]), .nPRE(nPRE[7]), .nCLR(nCLR[7]));  // open: nQ
  D_FlipFlop_Des d_flipflop_des_26 (
    .D(Entrada[6]), .CLK(CLK), .Q(Salida[6]), .nPRE(nPRE[6]), .nCLR(nCLR[6]));  // open: nQ
  D_FlipFlop_Des d_flipflop_des_27 (
    .D(Entrada[5]), .CLK(CLK), .Q(Salida[5]), .nPRE(nPRE[5]), .nCLR(nCLR[5]));  // open: nQ
  D_FlipFlop_Des d_flipflop_des_28 (
    .D(Entrada[4]), .CLK(CLK), .Q(Salida[4]), .nPRE(nPRE[4]), .nCLR(nCLR[4]));  // open: nQ
  D_FlipFlop_Des d_flipflop_des_29 (
    .D(Entrada[3]), .CLK(CLK), .Q(Salida[3]), .nPRE(nPRE[3]), .nCLR(nCLR[3]));  // open: nQ
  D_FlipFlop_Des d_flipflop_des_30 (
    .D(Entrada[2]), .CLK(CLK), .Q(Salida[2]), .nPRE(nPRE[2]), .nCLR(nCLR[2]));  // open: nQ
  D_FlipFlop_Des d_flipflop_des_31 (
    .D(Entrada[1]), .CLK(CLK), .Q(Salida[1]), .nPRE(nPRE[1]), .nCLR(nCLR[1]));  // open: nQ
  D_FlipFlop_Des d_flipflop_des_32 (
    .D(Entrada[0]), .CLK(CLK), .Q(Salida[0]), .nPRE(nPRE[0]), .nCLR(nCLR[0]));  // open: nQ
endmodule

module Register_8_bits_Hold___Paralel_Load (
  input  [7:0] nPRE,
  input  [7:0] Entrada,
  input  LOAD,
  input  CLK,
  input  [7:0] nCLR,
  output [7:0] Salida
);

  wire [7:0] multiplexer_1_out;

  Multiplexer #(.width(8), .enable("false")) multiplexer_1 (
    .in1(Entrada), .out(multiplexer_1_out), .sel(LOAD));  // open: in0
  Register_4_bits_Des register_4_bits_des_1 (
    .Entrada(multiplexer_1_out[3:0]), .CLK(CLK), .Salida(Salida[3:0]), .nPRE(nPRE[3:0]), .nCLR(nCLR[3:0]));
  Register_4_bits_Des register_4_bits_des_2 (
    .Entrada(multiplexer_1_out[7:4]), .CLK(CLK), .Salida(Salida[7:4]), .nPRE(nPRE[7:4]), .nCLR(nCLR[7:4]));
endmodule

module Register_4_bits_Des (
  input  [3:0] nPRE,
  input  [3:0] Entrada,
  input  CLK,
  input  [3:0] nCLR,
  output [3:0] Salida
);

  D_FlipFlop_Des d_flipflop_des_1 (
    .D(Entrada[3]), .CLK(CLK), .Q(Salida[3]), .nPRE(nPRE[3]), .nCLR(nCLR[3]));  // open: nQ
  D_FlipFlop_Des d_flipflop_des_2 (
    .D(Entrada[2]), .CLK(CLK), .Q(Salida[2]), .nPRE(nPRE[2]), .nCLR(nCLR[2]));  // open: nQ
  D_FlipFlop_Des d_flipflop_des_3 (
    .D(Entrada[1]), .CLK(CLK), .Q(Salida[1]), .nPRE(nPRE[1]), .nCLR(nCLR[1]));  // open: nQ
  D_FlipFlop_Des d_flipflop_des_4 (
    .D(Entrada[0]), .CLK(CLK), .Q(Salida[0]), .nPRE(nPRE[0]), .nCLR(nCLR[0]));  // open: nQ
endmodule

module MBR_EN (
  input  [7:0] in_1,
  input  MRB,
  input  MBRU,
  output [31:0] Salida_Signada,
  output [31:0] Salida_No_Signada
);

  assign Salida_Signada = MRB ? {{25{in_1[7]}}, in_1[6:0]} : 32'bz;  // Controlled_Buffer controlled_buffer_1
  assign Salida_No_Signada = MBRU ? {{24{1'b0}}, in_1} : 32'bz;  // Controlled_Buffer controlled_buffer_2
endmodule

module D_FlipFlop_Des (
  input  nPRE,
  input  D,
  input  CLK,
  input  nCLR,
  output Q,
  output nQ
);

  wire d_latch_1_q, not_1_out;

  D_Latch d_latch_1 (.nPRE(nPRE), .D(D), .Q(d_latch_1_q), .CLK(CLK), .nCLR(nCLR));  // open: nQ
  not not_1 (not_1_out, CLK);
  D_Latch d_latch_2 (.nPRE(nPRE), .D(d_latch_1_q), .Q(Q), .CLK(not_1_out), .nQ(nQ), .nCLR(nCLR));
endmodule

module D_FlipFlop_Asc (
  input  nPRE,
  input  D,
  input  CLK,
  input  nCLR,
  output Q,
  output nQ
);

  wire d_latch_1_q, not_1_out;

  not not_1 (not_1_out, CLK);
  D_Latch d_latch_1 (.nPRE(nPRE), .D(D), .Q(d_latch_1_q), .CLK(not_1_out), .nCLR(nCLR));  // open: nQ
  D_Latch d_latch_2 (.nPRE(nPRE), .D(d_latch_1_q), .Q(Q), .CLK(CLK), .nQ(nQ), .nCLR(nCLR));
endmodule

module D_Latch (
  input  nPRE,
  input  D,
  input  CLK,
  input  nCLR,
  output Q,
  output nQ
);

  wire nand_1_out, nand_2_out, not_1_out;

  not not_1 (not_1_out, D);
  nand nand_1 (nand_1_out, D, CLK);
  nand nand_2 (nand_2_out, CLK, not_1_out);
  nand nand_3 (Q, nPRE, nand_1_out, nQ);
  nand nand_4 (nQ, Q, nand_2_out, nCLR);
endmodule

module ALU_1_bit (
  input  Cin,
  input  INVA,
  input  A,
  input  ENA,
  input  B,
  input  ENB,
  input  F0,
  input  F1,
  output Suma,
  output Cout
);

  wire and_1_out, and_2_out, and_3_out, and_4_out, and_5_out, and_6_out, not_1_out, not_2_out, not_3_out,
       not_4_out, sumador_completo_alu_1_s, unidad_logica_alu_1_and, unidad_logica_alu_1_not,
       unidad_logica_alu_1_or, xor_1_out;

  and and_1 (and_1_out, A, ENA);
  and and_2 (and_2_out, B, ENB);
  xor xor_1 (xor_1_out, INVA, and_1_out);
  not not_1 (not_1_out, F0);
  and and_3 (and_3_out, not_1_out, not_2_out);
  not not_2 (not_2_out, F1);
  not not_3 (not_3_out, F0);
  and and_4 (and_4_out, not_3_out, F1);
  and and_5 (and_5_out, F0, not_4_out);
  not not_4 (not_4_out, F1);
  and and_6 (and_6_out, F0, F1);
  Unidad_Logica__ALU unidad_logica_alu_1 (
    .AND(unidad_logica_alu_1_and), .A(xor_1_out), .OR(unidad_logica_alu_1_or), .B(and_2_out),
    .NOT(unidad_logica_alu_1_not), .EN1(and_3_out), .EN2(and_4_out), .EN3(and_5_out));
  Sumador_Completo__ALU sumador_completo_alu_1 (
    .Cin(Cin), .A(xor_1_out), .S(sumador_completo_alu_1_s), .B(and_2_out), .EN(and_6_out), .Cout(Cout));
  or or_1 (Suma, unidad_logica_alu_1_and, unidad_logica_alu_1_or, unidad_logica_alu_1_not, sumador_completo_alu_1_s);
endmodule

module Unidad_Logica__ALU (
  input  EN1,
  input  A,
  input  B,
  input  EN2,
  input  EN3,
  output AND,
  output OR,
  output NOT
);

  wire and_1_out, not_1_out, or_1_out;

  and and_1 (and_1_out, A, B);
  or or_1 (or_1_out, A, B);
  not not_1 (not_1_out, B);
  and and_2 (OR, or_1_out, EN2);
  and and_3 (NOT, not_1_out, EN3);
  and and_4 (AND, and_1_out, EN1);

  // Notes on the sheet:
  //   A+B
  //   /B
  //   AB
endmodule

module Sumador_Completo__ALU (
  input  Cin,
  input  A,
  input  B,
  input  EN,
  output S,
  output Cout
);

  wire and_1_out, and_2_out, xor_1_out, xor_2_out;

  and and_1 (and_1_out, A, EN, B);
  xor xor_1 (xor_1_out, A, B);
  and and_2 (and_2_out, xor_1_out, EN, Cin);
  or or_1 (Cout, and_1_out, and_2_out);
  xor xor_2 (xor_2_out, Cin, xor_1_out);
  and and_3 (S, xor_2_out, EN);
endmodule

module Desplazador (
  input  [31:0] Entrada,
  input  SRA1,
  input  SLL8,
  output [31:0] Salida
);

  wire and_1_out, and_2_out, and_3_out, and_4_out, and_5_out, and_6_out, and_7_out, and_8_out, and_9_out,
       and_10_out, and_11_out, and_12_out, and_13_out, and_14_out, and_15_out, and_16_out, and_17_out,
       and_19_out, and_20_out, and_22_out, and_24_out, and_25_out, and_26_out, and_28_out, and_29_out,
       and_30_out, and_32_out, and_34_out, and_35_out, and_37_out, and_38_out, and_39_out, and_41_out,
       and_43_out, and_44_out, and_46_out, and_47_out, and_49_out, and_50_out, and_51_out, and_53_out,
       and_55_out, and_57_out, and_58_out, and_59_out, and_61_out, and_62_out, and_64_out, and_65_out,
       and_67_out, and_68_out, and_70_out, and_71_out, and_73_out, and_74_out, and_76_out, and_77_out,
       and_79_out, and_81_out, and_82_out, and_83_out, and_85_out, and_87_out, nor_1_out, S0, S1, S2, S3, S4,
       S5, S6, S7, S8, S9, S10, S11, S12, S13, S14, S15, S16, S17, S18, S19, S20, S21, S22, S23;

  nor nor_1 (nor_1_out, SRA1, SLL8);
  and and_1 (and_1_out, SRA1, Entrada[31]);
  or or_1 (Salida[31], S23, and_2_out);
  and and_2 (and_2_out, Entrada[31], nor_1_out);
  and and_3 (and_3_out, SRA1, Entrada[30]);
  or or_2 (Salida[30], and_1_out, S22, and_4_out);
  and and_4 (and_4_out, Entrada[30], nor_1_out);
  and and_5 (and_5_out, SRA1, Entrada[29]);
  and and_6 (and_6_out, Entrada[29], nor_1_out);
  or or_3 (Salida[29], and_3_out, S21, and_6_out);
  and and_7 (and_7_out, SRA1, Entrada[28]);
  and and_8 (and_8_out, Entrada[28], nor_1_out);
  or or_4 (Salida[28], and_5_out, S20, and_8_out);
  and and_9 (and_9_out, SRA1, Entrada[27]);
  and and_10 (and_10_out, Entrada[27], nor_1_out);
  or or_5 (Salida[27], and_7_out, S19, and_10_out);
  and and_11 (and_11_out, Entrada[26], nor_1_out);
  and and_12 (and_12_out, SRA1, Entrada[26]);
  or or_6 (Salida[26], and_9_out, S18, and_11_out);
  and and_13 (and_13_out, SRA1, Entrada[25]);
  or or_7 (Salida[25], and_12_out, S17, and_14_out);
  and and_14 (and_14_out, Entrada[25], nor_1_out);
  and and_15 (and_15_out, SRA1, Entrada[24]);
  and and_16 (and_16_out, Entrada[24], nor_1_out);
  or or_8 (Salida[24], and_13_out, S16, and_16_out);
  and and_17 (and_17_out, Entrada[23], SRA1);
  and and_18 (S23, Entrada[23], SLL8);
  and and_19 (and_19_out, Entrada[23], nor_1_out);
  or or_9 (Salida[23], and_15_out, S15, and_19_out);
  and and_20 (and_20_out, Entrada[22], SRA1);
  and and_21 (S22, Entrada[22], SLL8);
  or or_10 (Salida[22], and_17_out, S14, and_22_out);
  and and_22 (and_22_out, Entrada[22], nor_1_out);
  and and_23 (S21, Entrada[21], SLL8);
  and and_24 (and_24_out, Entrada[21], SRA1);
  or or_11 (Salida[21], and_20_out, S13, and_25_out);
  and and_25 (and_25_out, Entrada[21], nor_1_out);
  and and_26 (and_26_out, Entrada[20], SRA1);
  and and_27 (S20, Entrada[20], SLL8);
  and and_28 (and_28_out, Entrada[20], nor_1_out);
  or or_12 (Salida[20], and_24_out, S12, and_28_out);
  and and_29 (and_29_out, Entrada[19], SRA1);
  and and_30 (and_30_out, Entrada[19], nor_1_out);
  and and_31 (S19, Entrada[19], SLL8);
  or or_13 (Salida[19], and_26_out, S11, and_30_out);
  and and_32 (and_32_out, Entrada[18], SRA1);
  and and_33 (S18, Entrada[18], SLL8);
  or or_14 (Salida[18], and_29_out, S10, and_34_out);
  and and_34 (and_34_out, Entrada[18], nor_1_out);
  and and_35 (and_35_out, Entrada[17], SRA1);
  and and_36 (S17, Entrada[17], SLL8);
  or or_15 (Salida[17], and_32_out, S9, and_37_out);
  and and_37 (and_37_out, Entrada[17], nor_1_out);
  and and_38 (and_38_out, Entrada[16], SRA1);
  and and_39 (and_39_out, Entrada[16], nor_1_out);
  and and_40 (S16, Entrada[16], SLL8);
  or or_16 (Salida[16], and_35_out, S8, and_39_out);
  and and_41 (and_41_out, Entrada[15], SRA1);
  and and_42 (S15, Entrada[15], SLL8);
  or or_17 (Salida[15], and_38_out, S7, and_43_out);
  and and_43 (and_43_out, Entrada[15], nor_1_out);
  and and_44 (and_44_out, Entrada[14], SRA1);
  and and_45 (S14, Entrada[14], SLL8);
  or or_18 (Salida[14], and_41_out, S6, and_46_out);
  and and_46 (and_46_out, Entrada[14], nor_1_out);
  and and_47 (and_47_out, Entrada[13], SRA1);
  and and_48 (S13, Entrada[13], SLL8);
  and and_49 (and_49_out, Entrada[13], nor_1_out);
  or or_19 (Salida[13], and_44_out, S5, and_49_out);
  and and_50 (and_50_out, Entrada[12], SRA1);
  and and_51 (and_51_out, Entrada[12], nor_1_out);
  and and_52 (S12, Entrada[12], SLL8);
  or or_20 (Salida[12], and_47_out, S4, and_51_out);
  and and_53 (and_53_out, Entrada[11], SRA1);
  and and_54 (S11, Entrada[11], SLL8);
  or or_21 (Salida[11], and_50_out, S3, and_55_out);
  and and_55 (and_55_out, Entrada[11], nor_1_out);
  and and_56 (S10, Entrada[10], SLL8);
  and and_57 (and_57_out, SRA1, Entrada[10]);
  or or_22 (Salida[10], and_53_out, S2, and_58_out);
  and and_58 (and_58_out, Entrada[10], nor_1_out);
  and and_59 (and_59_out, Entrada[9], SRA1);
  and and_60 (S9, Entrada[9], SLL8);
  and and_61 (and_61_out, Entrada[9], nor_1_out);
  or or_23 (Salida[9], and_57_out, S1, and_61_out);
  and and_62 (and_62_out, Entrada[8], SRA1);
  and and_63 (S8, Entrada[8], SLL8);
  and and_64 (and_64_out, Entrada[8], nor_1_out);
  or or_24 (Salida[8], and_59_out, S0, and_64_out);
  and and_65 (and_65_out, Entrada[7], SRA1);
  and and_66 (S7, Entrada[7], SLL8);
  or or_25 (Salida[7], and_62_out, and_67_out);
  and and_67 (and_67_out, Entrada[7], nor_1_out);
  and and_68 (and_68_out, Entrada[6], SRA1);
  and and_69 (S6, Entrada[6], SLL8);
  or or_26 (Salida[6], and_65_out, and_70_out);
  and and_70 (and_70_out, Entrada[6], nor_1_out);
  and and_71 (and_71_out, Entrada[5], SRA1);
  and and_72 (S5, Entrada[5], SLL8);
  and and_73 (and_73_out, Entrada[5], nor_1_out);
  or or_27 (Salida[5], and_68_out, and_73_out);
  and and_74 (and_74_out, Entrada[4], SRA1);
  and and_75 (S4, Entrada[4], SLL8);
  or or_28 (Salida[4], and_71_out, and_76_out);
  and and_76 (and_76_out, Entrada[4], nor_1_out);
  and and_77 (and_77_out, Entrada[3], SRA1);
  and and_78 (S3, Entrada[3], SLL8);
  or or_29 (Salida[3], and_74_out, and_79_out);
  and and_79 (and_79_out, Entrada[3], nor_1_out);
  and and_80 (S2, Entrada[2], SLL8);
  and and_81 (and_81_out, Entrada[2], SRA1);
  and and_82 (and_82_out, Entrada[2], nor_1_out);
  or or_30 (Salida[2], and_77_out, and_82_out);
  and and_83 (and_83_out, Entrada[1], SRA1);
  and and_84 (S1, Entrada[1], SLL8);
  and and_85 (and_85_out, Entrada[1], nor_1_out);
  or or_31 (Salida[1], and_81_out, and_85_out);
  and and_86 (S0, SLL8, Entrada[0]);
  and and_87 (and_87_out, Entrada[0], nor_1_out);
  or or_32 (Salida[0], and_83_out, and_87_out);
endmodule

module ALU_8_bit (
  input  A7,
  input  A6,
  input  A5,
  input  A4,
  input  A3,
  input  A2,
  input  A1,
  input  A0,
  input  B7,
  input  B6,
  input  B5,
  input  B4,
  input  B3,
  input  B2,
  input  B1,
  input  B0,
  input  F0,
  input  F1,
  input  ENB,
  input  ENA,
  input  INVA,
  input  Cin,
  output Output,
  output Output_2,
  output Output_3,
  output Output_4,
  output Output_5,
  output Output_6,
  output Output_7,
  output Output_8,
  output Cout
);

  wire alu_1_bit_1_cout, alu_1_bit_2_cout, alu_1_bit_3_cout, alu_1_bit_4_cout, alu_1_bit_5_cout,
       alu_1_bit_6_cout, alu_1_bit_7_cout;

  ALU_1_bit alu_1_bit_1 (
    .Cin(Cin), .INVA(INVA), .A(A0), .Suma(Output), .ENA(ENA), .B(B0), .ENB(ENB), .F0(F0),
    .Cout(alu_1_bit_1_cout), .F1(F1));
  ALU_1_bit alu_1_bit_2 (
    .Cin(alu_1_bit_1_cout), .INVA(INVA), .A(A1), .Suma(Output_2), .ENA(ENA), .B(B1), .ENB(ENB), .F0(F0),
    .Cout(alu_1_bit_2_cout), .F1(F1));
  ALU_1_bit alu_1_bit_3 (
    .Cin(alu_1_bit_2_cout), .INVA(INVA), .A(A2), .Suma(Output_3), .ENA(ENA), .B(B2), .ENB(ENB), .F0(F0),
    .Cout(alu_1_bit_3_cout), .F1(F1));
  ALU_1_bit alu_1_bit_4 (
    .Cin(alu_1_bit_3_cout), .INVA(INVA), .A(A3), .Suma(Output_4), .ENA(ENA), .B(B3), .ENB(ENB), .F0(F0),
    .Cout(alu_1_bit_4_cout), .F1(F1));
  ALU_1_bit alu_1_bit_5 (
    .Cin(alu_1_bit_4_cout), .INVA(INVA), .A(A4), .Suma(Output_5), .ENA(ENA), .B(B4), .ENB(ENB), .F0(F0),
    .Cout(alu_1_bit_5_cout), .F1(F1));
  ALU_1_bit alu_1_bit_6 (
    .Cin(alu_1_bit_5_cout), .INVA(INVA), .A(A5), .Suma(Output_6), .ENA(ENA), .B(B5), .ENB(ENB), .F0(F0),
    .Cout(alu_1_bit_6_cout), .F1(F1));
  ALU_1_bit alu_1_bit_7 (
    .Cin(alu_1_bit_6_cout), .INVA(INVA), .A(A6), .Suma(Output_7), .ENA(ENA), .B(B6), .ENB(ENB), .F0(F0),
    .Cout(alu_1_bit_7_cout), .F1(F1));
  ALU_1_bit alu_1_bit_8 (
    .Cin(alu_1_bit_7_cout), .INVA(INVA), .A(A7), .Suma(Output_8), .ENA(ENA), .B(B7), .ENB(ENB), .F0(F0),
    .Cout(Cout), .F1(F1));
endmodule

// ALU 32
module ALU_32_bit (
  input  Cin,
  input  F0,
  input  F1,
  input  ENB,
  input  ENA,
  input  INVA,
  input  [31:0] A,
  input  [31:0] B,
  output [31:0] Output,
  output Z,
  output N,
  output Cout
);

  wire alu_8_bit_1_cout, alu_8_bit_2_cout, alu_8_bit_3_cout;

  ALU_8_bit alu_8_bit_1 (
    .A7(A[7]), .A6(A[6]), .A5(A[5]), .A4(A[4]), .A3(A[3]), .A2(A[2]), .A1(A[1]), .A0(A[0]), .B7(B[7]),
    .B6(B[6]), .B5(B[5]), .B4(B[4]), .B3(B[3]), .B2(B[2]), .B1(B[1]), .B0(B[0]), .F0(F0), .F1(F1), .ENB(ENB),
    .ENA(ENA), .INVA(INVA), .Cin(Cin), .Cout(alu_8_bit_1_cout), .Output(Output[0]), .Output_2(Output[1]),
    .Output_3(Output[2]), .Output_4(Output[3]), .Output_5(Output[4]), .Output_6(Output[5]),
    .Output_7(Output[6]), .Output_8(Output[7]));
  ALU_8_bit alu_8_bit_2 (
    .A7(A[15]), .A6(A[14]), .A5(A[13]), .A4(A[12]), .A3(A[11]), .A2(A[10]), .A1(A[9]), .A0(A[8]), .B7(B[15]),
    .B6(B[14]), .B5(B[13]), .B4(B[12]), .B3(B[11]), .B2(B[10]), .B1(B[9]), .B0(B[8]), .F0(F0), .F1(F1),
    .ENB(ENB), .ENA(ENA), .INVA(INVA), .Cin(alu_8_bit_1_cout), .Cout(alu_8_bit_2_cout), .Output(Output[8]),
    .Output_2(Output[9]), .Output_3(Output[10]), .Output_4(Output[11]), .Output_5(Output[12]),
    .Output_6(Output[13]), .Output_7(Output[14]), .Output_8(Output[15]));
  ALU_8_bit alu_8_bit_3 (
    .A7(A[23]), .A6(A[22]), .A5(A[21]), .A4(A[20]), .A3(A[19]), .A2(A[18]), .A1(A[17]), .A0(A[16]),
    .B7(B[23]), .B6(B[22]), .B5(B[21]), .B4(B[20]), .B3(B[19]), .B2(B[18]), .B1(B[17]), .B0(B[16]), .F0(F0),
    .F1(F1), .ENB(ENB), .ENA(ENA), .INVA(INVA), .Cin(alu_8_bit_2_cout), .Cout(alu_8_bit_3_cout),
    .Output(Output[16]), .Output_2(Output[17]), .Output_3(Output[18]), .Output_4(Output[19]),
    .Output_5(Output[20]), .Output_6(Output[21]), .Output_7(Output[22]), .Output_8(Output[23]));
  ALU_8_bit alu_8_bit_4 (
    .A7(A[31]), .A6(A[30]), .A5(A[29]), .A4(A[28]), .A3(A[27]), .A2(A[26]), .A1(A[25]), .A0(A[24]),
    .B7(B[31]), .B6(B[30]), .B5(B[29]), .B4(B[28]), .B3(B[27]), .B2(B[26]), .B1(B[25]), .B0(B[24]), .F0(F0),
    .F1(F1), .ENB(ENB), .ENA(ENA), .INVA(INVA), .Cin(alu_8_bit_3_cout), .Cout(Cout), .Output(Output[24]),
    .Output_2(Output[25]), .Output_3(Output[26]), .Output_4(Output[27]), .Output_5(Output[28]),
    .Output_6(Output[29]), .Output_7(Output[30]), .Output_8(N));
  nor nor_1 (Z, N, Output[30], Output[29], Output[28], Output[27], Output[26], Output[25], Output[24], Output[23], Output[22], Output[21], Output[20], Output[19], Output[18], Output[17], Output[16], Output[14], Output[13], Output[12], Output[11], Output[10], Output[9], Output[8], Output[7], Output[6], Output[5], Output[4], Output[3], Output[2], Output[1], Output[0], Output[15]);

  assign Output[31] = N;
endmodule

module MAR (
  input  [31:0] inp,
  output [31:0] out
);


  assign out = {inp[29:0], 2'b00};
endmodule
